# Fritzing sketch trashcollection (saved by Fritzing 0.9.2b)
circuit board: 8.46667cm x 5.64444cm
breadboards: 1

parts:
  R1 = Resistor [tolerance=±5% resistance=220 package=THT]
  R2 = Resistor [tolerance=±5% resistance=220 package=THT]
  R3 = Resistor [tolerance=±5% resistance=220 package=THT]
  S1 = Pushbutton [package="[THT]"]
  LED1 = LED - 3mm [color="Red (633nm)" current=10mA package="3 mm [THT]"]
  LED2 = LED - 3mm [color="Yellow (595nm)" package="3 mm [THT]"]
  LED3 = LED - 3mm [color="Green (570nm)" package="3 mm [THT]"]
  LED5 = LED - 3mm [color="White (4500K)" package="3 mm [THT]"]
  R5 = Resistor [tolerance=±5% resistance=470 package=THT]
  Raspberry_Pi1 = Raspberry Pi 2
  Q1 = NPN-Transistor [package="TO92 [THT]"]
  R6 = Resistor [tolerance=±5% resistance=22k package=THT]
  R7 = Resistor [tolerance=±5% resistance=10k package=THT]
  R8 = Resistor [tolerance=±2% resistance=1k package=THT]

nets:
  N1: R1.Pin_0, LED1.anode
  N2: R1.Pin_1, Raspberry_Pi1.GIPO15
  N3: R2.Pin_0, LED2.anode
  N4: R2.Pin_1, Raspberry_Pi1.GIPO24
  N5: R3.Pin_0, LED3.anode
  N6: R3.Pin_1, Raspberry_Pi1.GIPO7
  N7: S1.Pin_1, S1.Pin_2, R7.Pin_0, R8.Pin_1
  3V3: S1.Pin_3, S1.Pin_4, Raspberry_Pi1.3v3, Raspberry_Pi1.3V3
  N8: LED1.cathode, LED2.cathode, LED3.cathode, Raspberry_Pi1.GND, Q1.E, R7.Pin_1
  N9: LED5.cathode, Q1.C
  N10: LED5.anode, R5.Pin_1
  N11: R5.Pin_0, Raspberry_Pi1.5V
  N12: Raspberry_Pi1.GIPO21, R8.Pin_0
  N13: Raspberry_Pi1.ID_SC, R6.Pin_0
  N14: Q1.B, R6.Pin_1
